// Logisim project Calculadora Binária.circ as structural Verilog: 10 circuits, main circuit MeioSomador
module MeioSomador (
  input  A,
  input  B,
  input  in_3,
  output S,
  output Co
);

  and and_1 (Co, A, B);
  xor xor_1 (S, A, B);
endmodule

module Somador (
  input  A,
  input  B,
  input  CI,
  output s,
  output CO
);

  wire meiosomador_1_co, meiosomador_1_s, meiosomador_2_co;

  MeioSomador meiosomador_1 (.A(A), .B(B), .S(meiosomador_1_s), .Co(meiosomador_1_co));  // open: in_3
  MeioSomador meiosomador_2 (.A(CI), .B(meiosomador_1_s), .S(s), .Co(meiosomador_2_co));  // open: in_3
  or or_1 (CO, meiosomador_1_co, meiosomador_2_co);
endmodule

module Somador2Bits (
  input  A0,
  input  B0,
  input  A1,
  input  B1,
  output S0,
  output S1,
  output Co
);

  wire somador_1_co;

  Somador somador_1 (.A(A0), .B(B0), .CI(1'b0), .s(S0), .CO(somador_1_co));
  Somador somador_2 (.A(A1), .B(B1), .CI(somador_1_co), .s(S1), .CO(Co));
endmodule

module MeioSubtrator (
  input  A,
  input  B,
  output D,
  output Bo
);

  wire not_1_out;

  not not_1 (not_1_out, A);
  xor xor_1 (D, A, B);
  and and_1 (Bo, not_1_out, B);
endmodule

module Subtrator (
  input  A,
  input  B,
  input  BO_i,
  output DI_o,
  output BO_o
);

  wire meiosubtrator_1_bo, meiosubtrator_1_d, meiosubtrator_2_bo;

  MeioSubtrator meiosubtrator_1 (.A(A), .B(B), .D(meiosubtrator_1_d), .Bo(meiosubtrator_1_bo));
  MeioSubtrator meiosubtrator_2 (.A(meiosubtrator_1_d), .B(BO_i), .D(DI_o), .Bo(meiosubtrator_2_bo));
  or or_1 (BO_o, meiosubtrator_1_bo, meiosubtrator_2_bo);
endmodule

module Subtrator2Bits (
  input  A0,
  input  B0,
  input  A1,
  input  B1,
  output S,
  output S0,
  output Bo
);

  wire subtrator_1_bo_o;

  Subtrator subtrator_1 (.A(A0), .B(B0), .BO_i(1'b0), .DI_o(S0), .BO_o(subtrator_1_bo_o));
  Subtrator subtrator_2 (.A(A1), .B(B1), .BO_i(subtrator_1_bo_o), .DI_o(S), .BO_o(Bo));
endmodule

module multiplicador2Bitis (
  input  A1,
  input  A0,
  input  B1,
  input  B0,
  output S3,
  output S2,
  output S1,
  output S0
);

  wire and_2_out, and_3_out, and_4_out, not_1_out;

  and and_1 (S0, A0, B0);
  and and_2 (and_2_out, A0, B1);
  and and_3 (and_3_out, A1, B0);
  and and_4 (and_4_out, A1, B1);
  not not_1 (not_1_out, S0);
  and and_5 (S3, S0, and_4_out);
  xor xor_1 (S1, and_2_out, and_3_out);
  and and_6 (S2, not_1_out, and_4_out);
endmodule

module Mux2_1 (
  input  Soma,
  input  Seletor,
  input  Sub,
  output S
);

  wire and_1_out, and_2_out, not_1_out;

  not not_1 (not_1_out, Seletor);
  and and_1 (and_1_out, Soma, not_1_out);
  and and_2 (and_2_out, Seletor, Sub);
  or or_1 (S, and_1_out, and_2_out);
endmodule

module Mux4_1 (
  input  Soma,
  input  Sub,
  input  Seletor,
  input  Seletor2,
  input  Mult,
  input  Div,
  output out_7
);

  wire mux2_1_1_s, mux2_1_2_s;

  Mux2_1 mux2_1_1 (.Soma(Soma), .Seletor(Seletor), .Sub(Sub), .S(mux2_1_1_s));
  Mux2_1 mux2_1_2 (.Soma(Mult), .Seletor(Seletor), .Sub(Div), .S(mux2_1_2_s));
  Mux2_1 mux2_1_3 (.Soma(mux2_1_1_s), .Seletor(Seletor2), .Sub(mux2_1_2_s), .S(out_7));
endmodule

module calculadoraFinal (
  input  AO,
  input  B0,
  input  A1,
  input  B1,
  input  Seletor0,
  input  seletor1,
  output out_7,
  output out_8,
  output out_9
);

  wire multiplicador2bitis_1_s1, multiplicador2bitis_1_s2, multiplicador2bitis_1_s3, somador2bits_1_co,
       somador2bits_1_s0, somador2bits_1_s1, subtrator2bits_1_bo, subtrator2bits_1_s, subtrator2bits_1_s0,
       subtrator2bits_2_bo, subtrator2bits_2_s, subtrator2bits_2_s0;

  Somador2Bits somador2bits_1 (
    .A0(AO), .B0(A1), .A1(A1), .B1(B1), .S0(somador2bits_1_s0), .S1(somador2bits_1_s1), .Co(somador2bits_1_co));
  Subtrator2Bits subtrator2bits_1 (
    .A0(AO), .B0(A1), .A1(A1), .B1(B1), .S(subtrator2bits_1_s), .S0(subtrator2bits_1_s0),
    .Bo(subtrator2bits_1_bo));
  multiplicador2Bitis multiplicador2bitis_1 (
    .A1(AO), .A0(A1), .B0(B1), .S3(multiplicador2bitis_1_s3), .S2(multiplicador2bitis_1_s2),
    .S1(multiplicador2bitis_1_s1));  // open: B1, S0
  Subtrator2Bits subtrator2bits_2 (
    .A0(AO), .B0(A1), .A1(A1), .B1(B1), .S(subtrator2bits_2_s), .S0(subtrator2bits_2_s0),
    .Bo(subtrator2bits_2_bo));
  Mux4_1 mux4_1_1 (
    .Soma(somador2bits_1_s0), .Sub(subtrator2bits_1_s), .Seletor(Seletor0), .Seletor2(seletor1),
    .Mult(multiplicador2bitis_1_s3), .Div(subtrator2bits_2_s), .out_7(out_7));
  Mux4_1 mux4_1_2 (
    .Soma(somador2bits_1_s1), .Sub(subtrator2bits_1_s0), .Seletor(Seletor0), .Seletor2(seletor1),
    .Mult(multiplicador2bitis_1_s2), .Div(subtrator2bits_2_s0), .out_7(out_8));
  Mux4_1 mux4_1_3 (
    .Soma(somador2bits_1_co), .Sub(subtrator2bits_1_bo), .Seletor(Seletor0), .Seletor2(seletor1),
    .Mult(multiplicador2bitis_1_s1), .Div(subtrator2bits_2_bo), .out_7(out_9));

  assign B0 = A1;
endmodule
